# Fritzing sketch Diagram Pet (saved by Fritzing 1.0.4)
breadboards: 1

parts:
  U1 = LuaNode32 / ESP32 [part_number=ESP32S-PIN30]
  J1 = Basic Servo
  J2 = Piezo Speaker

nets:
  N1: U1.D13, J1.pulse
  GND: U1.GND, J1.gnd, J2.pin1
  VIN: U1.Vin, J1.vcc
  N2: U1.D5, J2.pin2

custom parts:
  LuaNode32 / ESP32: New Image for LuaNode32 DOIT ESP32 DEVKIT V1. Base parts from LuaNode32 / ESP32 ESP32 based LuaNode32 by G.Noorlander DOIT Esp32 DevKit v1 (30 pins long, 11 pins width) by Werner Rothschopf (modified by vanepp Dec 2018)
